# Fritzing sketch control_unit (saved by Fritzing 1.0.4)

parts:
  LCD2004-I2C1 = LCD2004-I2C
  M1 = pcf8574 io expansion board [package=THT]
  M2 = pcf8574 io expansion board [package=THT]
  M3 = pcf8574 io expansion board [package=THT]
  Keypad_4x4 = Keypad Membran 4x4
  A1 = GT-U7 NEO6M GPS
  Mod1 = ossoyoo-lora-module
  U1 = LM2596 step down module
  VCC1 = Battery block 9V [internal_resistance=0.1Ω]
  LLC2 = Logic Level Converter [package="Breakout board"]
  U2 = 16-Channel Relay Module [package=relay-16ch]
  J1 = male pin header, 13 pins [form="♂ (male)"]
  J2 = male pin header, 13 pins [form="♂ (male)"]
  J3 = male pin header, 13 pins [form="♂ (male)"]
  J4 = male pin header, 13 pins [form="♂ (male)"]
  J5 = male pin header, 2 pins [form="♂ (male)"]
  LED1 = LED - 3mm [color="Green (570nm)" current=0.030A package="3 mm [THT]"]
  LED2 = LED - 3mm [color="Yellow (574nm)" current=0.030A package="3 mm [THT]"]
  LED3 = LED - 3mm [color="Red (633nm)" current=0.030A package="3 mm [THT]"]
  LED4 = LED - 3mm [color="Blue (470nm)" current=0.030A package="3 mm [THT]"]
  R1 = Resistor [tolerance=±5% power=0.25W resistance=1k package=THT]
  R2 = Resistor [tolerance=±5% power=0.25W resistance=1k package=THT]
  R3 = Resistor [tolerance=±5% power=0.25W resistance=1k package=THT]
  R4 = Resistor [tolerance=±5% power=0.25W resistance=1k package=THT]
  R5 = Resistor [tolerance=±5% power=0.25W resistance=1k package=THT]
  LED5 = LED - 3mm [color="White (6500K)" current=0.030A package="3 mm [THT]"]

nets:
  GND: LCD2004-I2C1.GND, M1.GND, M2.GND, M3.GND, A1.Pin_4, Mod1.M0, Mod1.M1, Mod1.GND, U1.IN-, U1.OUT-, VCC1.-, LLC2.L-GND, LLC2.H-GND, U2.GND, U2.OUT_GND, J1.pin5, J5.pin2, LED1.cathode, LED2.cathode, LED3.cathode, LED4.cathode, LED5.cathode
  VCC: LCD2004-I2C1.VCC, M1.VCC, M2.VCC, M3.VCC, Mod1.VCC, U1.OUT+, LLC2.HV, U2.VCC, J5.pin1
  N1: LCD2004-I2C1.SDA, M1.SDA, M2.SDA, M3.SDA, LLC2.HV1
  N2: LCD2004-I2C1.SCL, M1.SCL, M2.SCL, M3.SCL, LLC2.HV2
  N3: M1.A2c, M1.A2-
  N4: M1.A1c, M1.A1-
  N5: M1.A0c, M1.A0-
  N6: M1.O0, U2.IN8
  N7: M1.O1, U2.IN7
  N8: M1.O2, U2.IN6
  N9: M1.O3, U2.IN5
  N10: M1.O4, U2.IN4
  N11: M1.O5, U2.IN3
  N12: M1.O6, U2.IN2
  N13: M1.O7, U2.IN1
  N14: M2.A2c, M2.A2-
  N15: M2.A1c, M2.A1-
  N16: M2.A0+, M2.A0c
  N17: M2.O0, U2.IN16
  N18: M2.O1, U2.IN15
  N19: M2.O2, U2.IN14
  N20: M2.O3, U2.IN13
  N21: M2.O4, U2.IN12
  N22: M2.O5, U2.IN11
  N23: M2.O6, U2.IN10
  N24: M2.O7, U2.IN9
  N25: M3.A2c, M3.A2-
  N26: M3.A1+, M3.A1c
  N27: M3.A0c, M3.A0-
  N28: M3.O0, Keypad_4x4.Pin8
  N29: M3.O1, Keypad_4x4.Pin7
  N30: M3.O2, Keypad_4x4.Pin6
  N31: M3.O3, Keypad_4x4.Pin5
  N32: M3.O4, Keypad_4x4.Pin4
  N33: M3.O5, Keypad_4x4.Pin3
  N34: M3.O6, Keypad_4x4.Pin2
  N35: M3.O7, Keypad_4x4.Pin1
  N36: A1.Pin_2, J1.pin3
  N37: A1.Pin_3, J1.pin2
  N38: A1.Pin_5, J3.pin3
  N39: Mod1.RXD, LLC2.HV4
  N40: Mod1.TXD, LLC2.HV3
  N41: U1.IN+, VCC1.+, U2.K12_COM, U2.K13_COM, U2.K14_COM, U2.K15_COM, U2.K16_COM
  N42: LLC2.LV1, J2.pin8
  N43: LLC2.LV2, J2.pin9
  N44: LLC2.LV, J1.pin1
  N45: LLC2.LV3, J4.pin11
  N46: LLC2.LV4, J4.pin12
  N47: U2.K12_NO, R1.Pin_0
  N48: U2.K13_NO, R2.Pin_0
  N49: U2.K14_NO, R3.Pin_0
  N50: U2.K15_NO, R4.Pin_0
  N51: U2.K16_NO, R5.Pin_0
  N52: LED1.anode, R1.Pin_1
  N53: LED2.anode, R2.Pin_1
  N54: LED3.anode, R3.Pin_1
  N55: LED4.anode, R4.Pin_1
  N56: R5.Pin_1, LED5.anode

notes:
  CN1
  CN2
  POWER
  +5V
  GND

custom parts:
  LCD2004-I2C: A standard character display with 4x20 characters. Comes in many colors with LCM2004 IIC attached.
  pcf8574 io expansion board: pcf8574 io expansion board.
  Keypad Membran 4x4: Membrane Keypad 4x4 Matrix
  GT-U7 NEO6M GPS: GT-U7 NEO6M GPS.
  ossoyoo-lora-module: Osoyoo Long Distance wireless transceiver Uart LoRa Module.
  LM2596 step down module: LM2596 DC-DC step down power supply module 3 A.
  Logic Level Converter: 5V to/from 3.3V logic level converter
  16-Channel Relay Module: 16 channel relay module
